# Fritzing sketch vending_machine (saved by Fritzing 0.9.3b)
breadboards: 1

parts:
  Part2 = Arduino Mega 2560 (Rev3)
  Part3 = TFT 2.8 inch 320x240 Touch w microSD [part_number=1770]  # not connected
  Part4 = Coin Acceptor - 6-Coin version
  J1 = Basic Servo
  J2 = Basic Servo
  J3 = Basic Servo
  J4 = Basic Servo
  R2 = Resistor [tolerance=±5% resistance=10k package=THT]
  J5 = ATX24 Pin Power Supply Connector [package=atx24_right_angle]

nets:
  N1: Part2.D21/SCL, Part4.SIG, R2.Pin_1
  GND: Part2.GND, Part4.GND, J1.gnd, J3.gnd, J4.gnd, J5.12V, J5.GND
  VIN: Part2.VIN, Part4.12V, R2.Pin_0
  N2: Part2.D45, J2.pulse
  N3: Part2.D46, J4.pulse
  N4: Part2.D50, J3.pulse
  N5: Part2.D52, J1.pulse
  VCC: J1.vcc, J3.vcc, J5.5V_STDBY

notes:
  Using a 2.8" TFTLCD Hat, wire le<module fritzingVersion="0.9.3b.04.19.5c895d327c44a3114e5fcc9d8260daf0cbb52806">
  <boundingRects>
  <boundingRect name="Breadboard View" rect="-6.72165 -256.5 202.443 90"/>
  <boundingRect name="Schematic View" rect="-117.438 -9.45018 99.8748 153.9"/>
  <boundingRect name="PCB View" rect="-116.635 -146.126 184.443 74.3279"/>
  </boundingRects>
  <instances>
  <instance modelIndex="85411615" moduleIdRef="SparkFun-Connectors-ATX24-RH" path="C:/Users/nicke/Downloads/fritzing.0.9.3b.64.pc/fritzing.0.9.3b.64.pc/fritzing-parts/core/sparkfun-connectors-atx24-rh.fzp">
  <title>J1</title>
  <views>
  <breadboardView layer="breadboard">
  <geometry x="-6.72165" y="-256.5" z="2.50001"/>
  <connectors>
  <connector connectorId="connector9" layer="breadboard">
  <geometry x="0" y="0"/>
  <connects/>
  </connector>
  <connector connectorId="connector2" layer="breadboard">
  <geometry x="0" y="0"/>
  <connects/>
  </connector>
  </connectors>
  </breadboardView>
  <pcbView layer="copper0">
  <geometry x="-116.635" y="-146.126" z="5.50001"/>
  <titleGeometry xOffset="184.443" x="67.8083" fontSize="5" yOffset="-7" textColor="#000000" y="-153.126" visible="true" z="13">
  <displayKey key=""/>
  </titleGeometry>
  <connectors>
  <connector connectorId="connector9" layer="copper0">
  <geometry x="0" y="0"/>
  <connects/>
  </connector>
  <connector connectorId="connector2" layer="copper0">
  <geometry x="0" y="0"/>
  <connects/>
  </connector>
  </connectors>
  </pcbView>
  <schematicView layer="schematic">
  <geometry x="-117.438" y="-9.45018" z="2.5"/>
  <titleGeometry xOffset="99.8748" x="-17.5629" fontSize="5" yOffset="-7" textColor="#000000" y="-16.4502" visible="true" z="7.00005">
  <displayKey key=""/>
  <displayKey key="part number"/>
  </titleGeometry>
  <connectors>
  <connector connectorId="connector9" layer="schematic">
  <geometry x="0" y="0"/>
  <connects/>
  </connector>
  <connector connectorId="connector2" layer="schematic">
  <geometry x="0" y="0"/>
  <connects/>
  </connector>
  <connector connectorId="connector18" layer="schematic">
  <geometry x="0" y="0"/>
  <connects/>
  </connector>
  </connectors>
  </schematicView>
  </views>
  </instance>
  </instances>
  </module>
  ads on Arduino Mega to HAT directly
  12V goes to the Coin Acceptor/powers the Arduino, 5V goes to the Servos
  Servo 1
  Servo 2
  Servo 3
  Servo 4

custom parts:
  TFT 2.8 inch 320x240 Touch w microSD: This TFT display is big (2.8" diagonal) bright (4 white-LED backlight) and colorful! 240x320 pixels with individual RGB pixel control. As a bonus, this display has a resistive touchscreen attached to it already, so you can detect finger presses anywhere on the screen.
  Coin Acceptor - 6-Coin version: 12V coin acceptor that can handle up to 6 different denominations. Output is either pulse width, serial, or single pin per coin value.
